// Logisim project TalosES_CTRL_card.circ as structural Verilog: 1 circuit, main circuit CTRL
module CTRL (
  input  [7:0] OPCODEIMM,
  input  CFH,
  input  SFH,
  input  ZFH,
  input  CFL,
  input  SFL,
  input  ZFL,
  input  nHLT,
  input  nRST,
  input  CLK,
  input  COMF,
  input  SIMF,
  output [7:0] IBH,
  output [7:0] IBL,
  output AHLE,
  output AR2LE,
  output IBLIOE,
  output RLOE,
  output AHOE,
  output AR2OE,
  output SFW,
  output ALLE,
  output BHLE,
  output SNH,
  output ALOE,
  output BHOE,
  output JAHLE,
  output SNL,
  output AR1CE,
  output BLLE,
  output JALLE,
  output nRD,
  output AR1LE,
  output BLOE,
  output PCOE,
  output nWR,
  output AR1OE,
  output EDBIE,
  output PCLE,
  output AR2CE,
  output IBHIOE,
  output RHOE,
  output OMF,
  output IMF
);

  wire CIMF, IMMHOE, IMMLOE, mnCLK, n7400_1_pin3, n7400_1_pin6, n7400_1_pin8, n7400_1_pin9, n7400_1_pin10,
       n7400_1_pin11, n7400_1_pin12, n7400_1_pin13, n7408_1_pin8, n7414_1_pin6, n7414_1_pin8, n7414_1_pin9,
       n7414_1_pin10, n7414_1_pin12, n7432_1_pin1, n7432_1_pin2, n7432_1_pin3, n7432_1_pin4, n7432_1_pin6,
       n7432_1_pin8, n7432_1_pin11, n7432_1_pin12, n7432_1_pin13, n7474_1_pin4, n7474_1_pin5, n7474_1_pin8,
       n7474_1_pin9, n7474_1_pin10, n7474_1_pin12, n7474_2_pin2, n7474_2_pin3, n7474_2_pin6, n7474_2_pin8,
       n7474_2_pin11, n7474_2_pin12, n74273_1_pin11, n74273_2_pin2, n74273_2_pin5, n74273_2_pin6,
       n74273_2_pin9, n74273_2_pin12, n74273_2_pin15, n74273_2_pin16, n74273_2_pin19, n74273_3_pin2,
       n74273_3_pin5, n74273_3_pin6, n74273_3_pin9, n74273_3_pin12, n74273_3_pin15, n74273_3_pin16,
       n74273_3_pin19, n74273_4_pin2, n74273_4_pin5, n74273_4_pin6, n74273_4_pin9, n74273_4_pin12,
       n74273_4_pin15, n74273_4_pin16, n74273_4_pin19, n74273_5_pin2, n74273_5_pin5, n74273_5_pin6,
       n74273_5_pin9, n74273_5_pin12, n74273_5_pin15, n74273_5_pin16, n74273_5_pin19, n74273_6_pin2,
       n74273_6_pin5, n74273_6_pin6, n74273_6_pin9, n74273_6_pin12, n74273_6_pin15, n74273_6_pin16,
       n74273_6_pin19, n74273_7_pin2, n74273_7_pin5, n74273_7_pin6, n74273_7_pin9, n74273_7_pin12,
       n74273_7_pin15, n74273_7_pin16, n74273_7_pin19, nCLK, nOE, plarom_1_p3, SOMF;
  wire [7:0] rom_1_data, rom_2_data, rom_3_data, rom_4_data;
  wire [15:8] n74273_1_pin2;

  _74273 u_74273_1 (
    .pin1(nRST), .pin2(n74273_1_pin2[8]), .pin3(OPCODEIMM[0]), .pin4(OPCODEIMM[1]), .pin5(n74273_1_pin2[9]),
    .pin6(n74273_1_pin2[10]), .pin7(OPCODEIMM[2]), .pin8(OPCODEIMM[3]), .pin9(n74273_1_pin2[11]),
    .pin19(n74273_1_pin2[15]), .pin18(OPCODEIMM[7]), .pin17(OPCODEIMM[6]), .pin16(n74273_1_pin2[14]),
    .pin15(n74273_1_pin2[13]), .pin14(OPCODEIMM[5]), .pin13(OPCODEIMM[4]), .pin12(n74273_1_pin2[12]),
    .pin11(n74273_1_pin11));
  ROM #(.addrWidth(16)) rom_1 (.addr({n74273_1_pin2, OMF, IMF, CFH, CFL, SFH, SFL, ZFH, ZFL}), .data(rom_1_data));
  _74273 u_74273_2 (
    .pin1(nRST), .pin2(n74273_2_pin2), .pin3(rom_1_data[0]), .pin4(rom_1_data[1]), .pin5(n74273_2_pin5),
    .pin6(n74273_2_pin6), .pin7(rom_1_data[2]), .pin8(rom_1_data[3]), .pin9(n74273_2_pin9),
    .pin19(n74273_2_pin19), .pin18(rom_1_data[7]), .pin17(rom_1_data[6]), .pin16(n74273_2_pin16),
    .pin15(n74273_2_pin15), .pin14(rom_1_data[5]), .pin13(rom_1_data[4]), .pin12(n74273_2_pin12),
    .pin11(mnCLK));
  Pull_Resistor pull_resistor_1 (.node(AHLE));
  Pull_Resistor pull_resistor_2 (.node(AHOE));
  Pull_Resistor pull_resistor_3 (.node(ALLE));
  Pull_Resistor pull_resistor_4 (.node(ALOE));
  Pull_Resistor pull_resistor_5 (.node(AR1CE));
  Pull_Resistor pull_resistor_6 (.node(AR1LE));
  Pull_Resistor pull_resistor_7 (.node(AR1OE));
  Pull_Resistor pull_resistor_8 (.node(AR2CE));
  IC74245 ic74245_1 (
    .DIR(1'b0), .iOE(nOE), .B0(n74273_2_pin19), .B1(n74273_2_pin16), .B2(n74273_2_pin15),
    .B3(n74273_2_pin12), .B4(n74273_2_pin9), .B5(n74273_2_pin6), .B6(n74273_2_pin5), .B7(n74273_2_pin2),
    .A0(AHLE), .A1(AHOE), .A2(ALLE), .A3(ALOE), .A4(AR1CE), .A5(AR1LE), .A6(AR1OE), .A7(AR2CE));
  ROM #(.addrWidth(16)) rom_2 (.addr({n74273_1_pin2, OMF, IMF, CFH, CFL, SFH, SFL, ZFH, ZFL}), .data(rom_2_data));
  _74273 u_74273_3 (
    .pin1(nRST), .pin2(n74273_3_pin2), .pin3(rom_2_data[0]), .pin4(rom_2_data[1]), .pin5(n74273_3_pin5),
    .pin6(n74273_3_pin6), .pin7(rom_2_data[2]), .pin8(rom_2_data[3]), .pin9(n74273_3_pin9),
    .pin19(n74273_3_pin19), .pin18(rom_2_data[7]), .pin17(rom_2_data[6]), .pin16(n74273_3_pin16),
    .pin15(n74273_3_pin15), .pin14(rom_2_data[5]), .pin13(rom_2_data[4]), .pin12(n74273_3_pin12),
    .pin11(mnCLK));
  Pull_Resistor pull_resistor_9 (.node(AR2LE));
  Pull_Resistor pull_resistor_10 (.node(AR2OE));
  Pull_Resistor pull_resistor_11 (.node(BHLE));
  Pull_Resistor pull_resistor_12 (.node(BHOE));
  Pull_Resistor pull_resistor_13 (.node(BLLE));
  Pull_Resistor pull_resistor_14 (.node(BLOE));
  Pull_Resistor pull_resistor_15 (.node(EDBIE));
  Pull_Resistor pull_resistor_16 (.node(IBHIOE));
  IC74245 ic74245_2 (
    .DIR(1'b0), .iOE(nOE), .B0(n74273_3_pin19), .B1(n74273_3_pin16), .B2(n74273_3_pin15),
    .B3(n74273_3_pin12), .B4(n74273_3_pin9), .B5(n74273_3_pin6), .B6(n74273_3_pin5), .B7(n74273_3_pin2),
    .A0(AR2LE), .A1(AR2OE), .A2(BHLE), .A3(BHOE), .A4(BLLE), .A5(BLOE), .A6(EDBIE), .A7(IBHIOE));
  ROM #(.addrWidth(16)) rom_3 (.addr({n74273_1_pin2, OMF, IMF, CFH, CFL, SFH, SFL, ZFH, ZFL}), .data(rom_3_data));
  _7474 u_7474_1 (
    .pin1(nRST), .pin2(nHLT), .pin3(nCLK), .pin4(n7474_1_pin4), .pin5(n7474_1_pin5), .pin6(nOE),
    .pin13(nRST), .pin12(n7474_1_pin12), .pin11(mnCLK), .pin10(n7474_1_pin10), .pin9(n7474_1_pin9),
    .pin8(n7474_1_pin8));
  _74273 u_74273_4 (
    .pin1(nRST), .pin2(n74273_4_pin2), .pin3(rom_3_data[0]), .pin4(rom_3_data[1]), .pin5(n74273_4_pin5),
    .pin6(n74273_4_pin6), .pin7(rom_3_data[2]), .pin8(rom_3_data[3]), .pin9(n74273_4_pin9),
    .pin19(n74273_4_pin19), .pin18(rom_3_data[7]), .pin17(rom_3_data[6]), .pin16(n74273_4_pin16),
    .pin15(n74273_4_pin15), .pin14(rom_3_data[5]), .pin13(rom_3_data[4]), .pin12(n74273_4_pin12),
    .pin11(mnCLK));
  Pull_Resistor pull_resistor_17 (.node(IBLIOE));
  Pull_Resistor pull_resistor_18 (.node(IMMHOE));
  Pull_Resistor pull_resistor_19 (.node(IMMLOE));
  Pull_Resistor pull_resistor_20 (.node(JAHLE));
  Pull_Resistor pull_resistor_21 (.node(JALLE));
  Pull_Resistor pull_resistor_22 (.node(PCOE));
  Pull_Resistor pull_resistor_23 (.node(PCLE));
  Pull_Resistor pull_resistor_24 (.node(RHOE));
  // PlaRom #(.Contents("2 1*8 2 1*6 2 2 1*8 2 1*5 2 1 2 1*6 2 2 1*5 0*6"), .\and (6), .outputs(1)) plarom_1: pin names not known; wires that end beside it: OPCODEIMM, 1'b0, plarom_1_p3
  _7408 u_7408_1 (
    .pin1(n7474_1_pin5), .pin2(nCLK), .pin3(mnCLK), .pin4(n7474_1_pin8), .pin5(plarom_1_p3),
    .pin6(n7474_1_pin12), .pin13(n7474_1_pin8), .pin12(mnCLK), .pin11(n74273_1_pin11), .pin10(n7474_1_pin9),
    .pin9(mnCLK), .pin8(n7408_1_pin8));
  IC74245 ic74245_3 (
    .DIR(1'b0), .iOE(nOE), .B0(n74273_4_pin19), .B1(n74273_4_pin16), .B2(n74273_4_pin15),
    .B3(n74273_4_pin12), .B4(n74273_4_pin9), .B5(n74273_4_pin6), .B6(n74273_4_pin5), .B7(n74273_4_pin2),
    .A0(IBLIOE), .A1(IMMHOE), .A2(IMMLOE), .A3(JAHLE), .A4(JALLE), .A5(PCOE), .A6(PCLE), .A7(RHOE));
  ROM #(.addrWidth(16)) rom_4 (.addr({n74273_1_pin2, OMF, IMF, CFH, CFL, SFH, SFL, ZFH, ZFL}), .data(rom_4_data));
  _74273 u_74273_5 (
    .pin1(nRST), .pin2(n74273_5_pin2), .pin3(rom_4_data[0]), .pin4(rom_4_data[1]), .pin5(n74273_5_pin5),
    .pin6(n74273_5_pin6), .pin7(rom_4_data[2]), .pin8(rom_4_data[3]), .pin9(n74273_5_pin9),
    .pin19(n74273_5_pin19), .pin18(rom_4_data[7]), .pin17(rom_4_data[6]), .pin16(n74273_5_pin16),
    .pin15(n74273_5_pin15), .pin14(rom_4_data[5]), .pin13(rom_4_data[4]), .pin12(n74273_5_pin12),
    .pin11(mnCLK));
  Pull_Resistor pull_resistor_25 (.node(RLOE));
  Pull_Resistor pull_resistor_26 (.node(SFW));
  Pull_Resistor pull_resistor_27 (.node(SNH));
  Pull_Resistor pull_resistor_28 (.node(SNL));
  Pull_Resistor pull_resistor_29 (.node(nRD));
  Pull_Resistor pull_resistor_30 (.node(nWR));
  Pull_Resistor pull_resistor_31 (.node(CIMF));
  Pull_Resistor pull_resistor_32 (.node(SOMF));
  IC74245 ic74245_4 (
    .DIR(1'b0), .iOE(nOE), .B0(n74273_5_pin19), .B1(n74273_5_pin16), .B2(n74273_5_pin15),
    .B3(n74273_5_pin12), .B4(n7400_1_pin6), .B5(n7400_1_pin3), .B6(n74273_5_pin5), .B7(n74273_5_pin2),
    .A0(RLOE), .A1(SFW), .A2(SNH), .A3(SNL), .A4(nRD), .A5(nWR), .A6(CIMF), .A7(SOMF));
  _7400 u_7400_1 (
    .pin1(CLK), .pin2(n74273_5_pin6), .pin3(n7400_1_pin3), .pin4(n74273_5_pin9), .pin5(n74273_5_pin9),
    .pin6(n7400_1_pin6), .pin13(n7400_1_pin13), .pin12(n7400_1_pin12), .pin11(n7400_1_pin11),
    .pin10(n7400_1_pin10), .pin9(n7400_1_pin9), .pin8(n7400_1_pin8));
  // NoConnect on n7400_1_pin11
  // NoConnect on n7400_1_pin8
  // NoConnect on n7432_1_pin11
  _7432 u_7432_1 (
    .pin1(n7432_1_pin1), .pin2(n7432_1_pin2), .pin3(n7432_1_pin3), .pin4(n7432_1_pin4), .pin5(nRST),
    .pin6(n7432_1_pin6), .pin13(n7432_1_pin13), .pin12(n7432_1_pin12), .pin11(n7432_1_pin11), .pin10(nRST),
    .pin9(COMF), .pin8(n7432_1_pin8));
  // NoConnect on n7432_1_pin3
  _7414 u_7414_1 (
    .pin1(CLK), .pin2(nCLK), .pin3(CIMF), .pin4(n7432_1_pin4), .pin5(SOMF), .pin6(n7414_1_pin6),
    .pin13(IMMLOE), .pin12(n7414_1_pin12), .pin11(IMMHOE), .pin10(n7414_1_pin10), .pin9(n7414_1_pin9),
    .pin8(n7414_1_pin8));
  _7474 u_7474_2 (
    .pin1(n7432_1_pin6), .pin2(n7474_2_pin2), .pin3(n7474_2_pin3), .pin4(SIMF), .pin5(IMF),
    .pin6(n7474_2_pin6), .pin13(n7432_1_pin8), .pin12(n7474_2_pin12), .pin11(n7474_2_pin11),
    .pin10(n7414_1_pin6), .pin9(OMF), .pin8(n7474_2_pin8));
  // NoConnect on n7474_2_pin6
  _74273 u_74273_6 (
    .pin1(nRST), .pin2(n74273_6_pin2), .pin3(OPCODEIMM[0]), .pin4(OPCODEIMM[1]), .pin5(n74273_6_pin5),
    .pin6(n74273_6_pin6), .pin7(OPCODEIMM[2]), .pin8(OPCODEIMM[3]), .pin9(n74273_6_pin9),
    .pin19(n74273_6_pin19), .pin18(OPCODEIMM[7]), .pin17(OPCODEIMM[6]), .pin16(n74273_6_pin16),
    .pin15(n74273_6_pin15), .pin14(OPCODEIMM[5]), .pin13(OPCODEIMM[4]), .pin12(n74273_6_pin12),
    .pin11(n7408_1_pin8));
  _74273 u_74273_7 (
    .pin1(nRST), .pin2(n74273_7_pin2), .pin3(n74273_6_pin2), .pin4(n74273_6_pin5), .pin5(n74273_7_pin5),
    .pin6(n74273_7_pin6), .pin7(n74273_6_pin6), .pin8(n74273_6_pin9), .pin9(n74273_7_pin9),
    .pin19(n74273_7_pin19), .pin18(n74273_6_pin19), .pin17(n74273_6_pin16), .pin16(n74273_7_pin16),
    .pin15(n74273_7_pin15), .pin14(n74273_6_pin15), .pin13(n74273_6_pin12), .pin12(n74273_7_pin12),
    .pin11(mnCLK));
  // NoConnect on n7414_1_pin8
  // NoConnect on n7474_2_pin8
  IC74245 ic74245_5 (
    .DIR(1'b0), .iOE(n7414_1_pin10), .B0(n74273_7_pin2), .B1(n74273_7_pin5), .B2(n74273_7_pin6),
    .B3(n74273_7_pin9), .B4(n74273_7_pin12), .B5(n74273_7_pin15), .B6(n74273_7_pin16), .B7(n74273_7_pin19),
    .A0(IBH[0]), .A1(IBH[1]), .A2(IBH[2]), .A3(IBH[3]), .A4(IBH[4]), .A5(IBH[5]), .A6(IBH[6]), .A7(IBH[7]));
  IC74245 ic74245_6 (
    .DIR(1'b0), .iOE(n7414_1_pin12), .B0(n74273_7_pin2), .B1(n74273_7_pin5), .B2(n74273_7_pin6),
    .B3(n74273_7_pin9), .B4(n74273_7_pin12), .B5(n74273_7_pin15), .B6(n74273_7_pin16), .B7(n74273_7_pin19),
    .A0(IBL[0]), .A1(IBL[1]), .A2(IBL[2]), .A3(IBL[3]), .A4(IBL[4]), .A5(IBL[5]), .A6(IBL[6]), .A7(IBL[7]));
  // also tied to GND on the sheet: {n7400_1_pin13, n7400_1_pin12, n7400_1_pin10, n7400_1_pin9, n7432_1_pin1, n7432_1_pin13, n7432_1_pin2, n7432_1_pin12, n7474_2_pin2, n7474_2_pin12, n7474_2_pin3, n7474_2_pin11, n7414_1_pin9}
  // also tied to VCC on the sheet: {n7474_1_pin4, n7474_1_pin10}

  // Notes on the sheet:
  //   AR2LE: pull=up
  //   AR2OE: pull=up
  //   BHLE: pull=up
  //   BHOE: pull=up
  //   BLLE: pull=up
  //   BLOE: pull=up
  //   EDBIE: pull=up
  //   IBHIOE: pull=up
  //   OPCODEIMM: pull=up
  //   IBLIOE: pull=up
  //   JAHLE: pull=up
  //   JALLE: pull=up
  //   PCOE: pull=up
  //   PCLE: pull=up
  //   RHOE: pull=up
  //   RLOE: pull=up
  //   SFW: pull=up
  //   SNH: pull=up
  //   SNL: pull=up
  //   nRD: pull=up
  //   nWR: pull=up
  //   nHLT: pull=up
  //   nRST: pull=up
  //   CLK: pull=up
  //   COMF: pull=up
  //   SIMF: pull=up
  //   IMF: pull=up
  //   OMF: pull=up
  //   IBH: pull=up
  //   IBL: pull=up
  //   CFH: pull=up
  //   CFL: pull=up
  //   SFH: pull=up
  //   SFL: pull=up
  //   ZFH: pull=up
  //   ZFL: pull=up
  //   AHLE: pull=up
  //   AHOE: pull=up
  //   ALLE: pull=up
  //   ALOE: pull=up
  //   AR1CE: pull=up
  //   AR1LE: pull=up
  //   AR1OE: pull=up
  //   AR2CE: pull=up
  //   IR
  //   This should be a 74HCT74N
  //   IMM1
  //   IMM2
endmodule
